# Fritzing sketch ibus-master-node (saved by Fritzing 0.9.3b)
circuit board: 8.46667cm x 5.64444cm
breadboards: 1

parts:
  IC1 = IC, DIP package, 8 pins [chip_label=2025]
  R1 = Resistor [tolerance=±5% resistance=1k package="0603 [SMD]"]
  JP1 = Header 2 [package=molex-1x2_lock]
  Part1 = Arduino Mega 2560 (Rev3)

nets (from the breadboard view):
  N1: IC1.pin1, R1.Pin_1
  N2: IC1.pin2, Part1.D2_PWM
  N3: IC1.pin3, Part1.GND
  N4: IC1.pin4, R1.Pin_0, JP1.1
  N5: IC1.pin5, Part1.D19/RX1
  N6: IC1.pin6, Part1.D18/TX1
  N7: IC1.pin8, Part1.5V
